# Fritzing sketch Flame_Alarm (saved by Fritzing 0.9.3b)

parts:
  Part1 = Arduino Uno (Rev3)
  Mod1 = KY-026 Flame Sensor Module [package="Breakout board"]
  J1 = Piezo Speaker
  M1 = DC Motor
  KY-1 = Keyes Relay [package=THT]
  JACK1 = 2.1mm Barrel Jack with Terminal Block
  J2 = Basic Servo

nets:
  N1: Part1.D8, J1.pin2
  N2: Part1.D9_PWM, KY-1.signal
  N3: Part1.D10_PWM/SS, J2.pulse
  N4: Part1.GND, J1.pin1
  N5: Part1.D2, Mod1.D0
  N6: Part1.5V, Mod1.+
  N7: M1.pin_1, JACK1.NEG
  N8: M1.pin_2, KY-1.NO
  N9: KY-1.C, JACK1.POS

notes:
  1.Tracking
  - Flame = HIGH
  - or gas = HIGH
  2. Fire
  - temp > 50
  - time > 30s
  3. Pump

custom parts:
  KY-026 Flame Sensor Module: KY-026 Flame Sensor Module reacts in the presence of fire.
  Keyes Relay: The Keyes 5V relay module is suitable for SCM development, home appliance control. It uses a 5V~12V TIL control signal which can control DC / AC signal.
